// Logisim project add1.circ as structural Verilog: 1 circuit, main circuit add
module add (
  input  A,
  input  B,
  input  SIN,
  output S,
  output cout
);

  wire and_1_out, and_2_out, and_3_out, not_1_out, not_2_out, not_3_out, xor_1_out;

  not not_1 (not_1_out, A);
  not not_2 (not_2_out, B);
  not not_3 (not_3_out, SIN);
  xor xor_1 (xor_1_out, A, B);
  and and_1 (and_1_out, A, B);
  and and_2 (and_2_out, A, not_3_out);
  and and_3 (and_3_out, B, SIN);
  xor xor_2 (S, xor_1_out, not_3_out);
  or or_1 (cout, and_1_out, and_3_out);
endmodule
