// Logisim project 38decoder.circ as structural Verilog: 2 circuits, main circuit main
module main (
  input  EN,
  input  A2,
  input  A1,
  input  A0,
  output Y7,
  output Y6,
  output Y5,
  output Y4,
  output Y3,
  output Y2,
  output Y1,
  output Y0
);

  wire not_1_out, or_1_out, or_2_out;

  not not_1 (not_1_out, A2);
  or or_1 (or_1_out, A2, EN);
  or or_2 (or_2_out, not_1_out, EN);
  decoder24 decoder24_1 (.A1(A1), .A0(A0), .EN(or_1_out), .Y3(Y3), .Y2(Y2), .Y1(Y1), .Y0(Y0));
  decoder24 decoder24_2 (.A1(A1), .A0(A0), .EN(or_2_out), .Y3(Y7), .Y2(Y6), .Y1(Y5), .Y0(Y4));
endmodule

module decoder24 (
  input  A1,
  input  A0,
  input  EN,
  output Y3,
  output Y2,
  output Y1,
  output Y0
);

  wire not_1_out, not_2_out;

  not not_1 (not_1_out, A1);
  not not_2 (not_2_out, A0);
  and and_1 (Y3, A1, A0, EN);
  and and_2 (Y2, A1, not_2_out, EN);
  and and_3 (Y1, not_1_out, A0, EN);
  and and_4 (Y0, not_1_out, not_2_out, EN);
endmodule
