// Logisim project 3位4选1选择器（错误）.circ as structural Verilog: 2 circuits, main circuit mux_1bit_4to1
module mux_1bit_4to1 (
  input  A3,
  input  A2,
  input  A1,
  input  A0,
  input  S0,
  input  S1,
  output Y
);

  wire and_1_out, and_2_out, and_3_out, and_4_out, not_1_out, not_2_out, not_3_out, not_4_out;

  not not_1 (not_1_out, S1);
  not not_2 (not_2_out, S0);
  not not_3 (not_3_out, S0);
  not not_4 (not_4_out, S1);
  and and_1 (and_1_out, A3, S0, S1);
  and and_2 (and_2_out, A2, S0, not_1_out);
  and and_3 (and_3_out, A1, not_2_out, S1);
  and and_4 (and_4_out, A0, not_3_out, not_4_out);
  and and_5 (Y, and_1_out, and_4_out);
endmodule

module mux_3bit_4to1 (
  input  [2:0] A_3,
  input  [2:0] B_2,
  input  [2:0] C_1,
  input  [2:0] D_0,
  input  S1,
  input  S0,
  output [2:0] Y
);

  mux_1bit_4to1 mux_1bit_4to1_1 (.A3(A_3[0]), .A2(B_2[0]), .A1(C_1[0]), .A0(D_0[0]), .S0(S1), .S1(S0), .Y(Y[0]));
  mux_1bit_4to1 mux_1bit_4to1_2 (.A3(A_3[1]), .A2(B_2[1]), .A1(C_1[1]), .A0(D_0[1]), .S0(S1), .S1(S0), .Y(Y[1]));
  mux_1bit_4to1 mux_1bit_4to1_3 (.A3(A_3[2]), .A2(B_2[2]), .A1(C_1[2]), .A0(D_0[2]), .S0(S1), .S1(S0), .Y(Y[2]));
endmodule
