// Logisim project Priority_Encode.circ as structural Verilog: 1 circuit, main circuit main
module main (
  input  in_1,
  input  in_2,
  input  in_3,
  input  in_4,
  output out_5,
  output out_6
);

  wire and_1_out, and_2_out, not_1_out, not_2_out, not_3_out, not_4_out;

  not not_1 (not_1_out, in_1);
  not not_2 (not_2_out, in_2);
  not not_3 (not_3_out, in_3);
  not not_4 (not_4_out, in_4);
  and and_1 (and_1_out, not_2_out, not_3_out, not_4_out);
  and and_2 (and_2_out, in_3, in_4);
  or or_1 (out_5, and_1_out, in_4);
  or or_2 (out_6, and_2_out, in_4);

  // Other names for the same wires on the sheet: A0 = in_1; A1 = in_2; A2 = in_3; A3 = in_4; Y0 = out_5; Y1 = out_6
endmodule
