// Logisim project add2.circ as structural Verilog: 5 circuits, main circuit add
module add (
  input  A,
  input  B,
  input  SIN,
  output S,
  output cout
);

  wire and_1_out, and_2_out, and_3_out, not_1_out, not_2_out, not_3_out, xor_1_out;

  not not_1 (not_1_out, A);
  not not_2 (not_2_out, B);
  not not_3 (not_3_out, SIN);
  xor xor_1 (xor_1_out, A, B);
  and and_1 (and_1_out, A, B);
  and and_2 (and_2_out, A, SIN);
  and and_3 (and_3_out, B, SIN);
  xor xor_2 (S, xor_1_out, SIN);
  or or_1 (cout, and_1_out, and_2_out, and_3_out);
endmodule

module four_add (
  input  A3,
  input  A2,
  input  A1,
  input  A0,
  input  B3,
  input  B2,
  input  B1,
  input  B0,
  output out_9,
  output out_10,
  output out_11,
  output out_12
);

  wire add_1_cout, add_2_cout, add_3_cout, add_4_cout;

  add add_1 (.B(B0), .A(A0), .S(out_9), .cout(add_1_cout));  // open: SIN
  add add_2 (.B(B1), .SIN(add_1_cout), .A(A1), .S(out_10), .cout(add_2_cout));
  add add_3 (.B(B2), .SIN(add_2_cout), .A(A2), .S(out_11), .cout(add_3_cout));
  add add_4 (.B(B3), .SIN(add_3_cout), .A(A3), .S(out_12), .cout(add_4_cout));
  LED led_1 (.in(add_4_cout));
endmodule

module A_Subtractor (
  input  A,
  input  B,
  input  BIN,
  output P,
  output BS
);

  wire and_1_out, and_2_out, and_3_out, not_1_out, not_2_out, not_3_out, xor_1_out;

  not not_1 (not_1_out, A);
  not not_2 (not_2_out, B);
  not not_3 (not_3_out, BIN);
  xor xor_1 (xor_1_out, A, B);
  and and_1 (and_1_out, not_1_out, B);
  and and_2 (and_2_out, not_1_out, BIN);
  and and_3 (and_3_out, B, BIN);
  xor xor_2 (P, xor_1_out, BIN);
  or or_1 (BS, and_1_out, and_2_out, and_3_out);

  // Notes on the sheet:
  //   BS= ¬A・B + ¬A・Bin + B・Bin
endmodule

module substractor_Four (
  input  A3,
  input  A2,
  input  A1,
  input  A0,
  input  B3,
  input  B2,
  input  B1,
  input  B0,
  output out_9,
  output out_10,
  output out_11,
  output out_12
);

  wire a_subtractor_1_bs, a_subtractor_2_bs, a_subtractor_3_bs, a_subtractor_4_bs;

  A_Subtractor a_subtractor_1 (.A(A0), .B(B0), .P(out_9), .BS(a_subtractor_1_bs));  // open: BIN
  A_Subtractor a_subtractor_2 (.A(A1), .B(B1), .BIN(a_subtractor_1_bs), .P(out_10), .BS(a_subtractor_2_bs));
  A_Subtractor a_subtractor_3 (.A(A2), .B(B2), .BIN(a_subtractor_2_bs), .P(out_11), .BS(a_subtractor_3_bs));
  A_Subtractor a_subtractor_4 (.A(A3), .B(B3), .BIN(a_subtractor_3_bs), .P(out_12), .BS(a_subtractor_4_bs));
  LED led_1 (.in(a_subtractor_4_bs));
endmodule

module Sign_Magnitude_Adder (
  input  A3,
  input  A2,
  input  A1,
  input  A0,
  input  B3,
  input  B2,
  input  B1,
  input  B0,
  output Y0,
  output Y1,
  output Y2,
  output Y3
);

  wire and_1_out, multiplexer_1_out, xor_1_out;
  wire [1:0] substractor_four_2_out_12;
  wire [2:0] four_add_1_out_9, multiplexer_3_out, substractor_four_1_out_9, substractor_four_2_out_9;

  xor xor_1 (xor_1_out, A3, B3);
  and and_1 (and_1_out, A3, B3);
  four_add four_add_1 (
    .A2(A2), .A1(A1), .A0(A0), .B2(B2), .B1(B1), .B0(B0), .out_9(four_add_1_out_9[0]),
    .out_10(four_add_1_out_9[1]), .out_11(four_add_1_out_9[2]));  // open: B3, A3, out_12
  substractor_Four substractor_four_1 (
    .A2(A2), .A1(A1), .A0(A0), .B2(B2), .B1(B1), .B0(B0), .out_9(substractor_four_1_out_9[0]),
    .out_10(substractor_four_1_out_9[1]), .out_11(substractor_four_1_out_9[2]),
    .out_12(substractor_four_2_out_12[1]));  // open: B3, A3
  substractor_Four substractor_four_2 (
    .A2(A2), .A1(A1), .A0(A0), .B2(B2), .B1(B1), .B0(B0), .out_9(substractor_four_2_out_9[0]),
    .out_10(substractor_four_2_out_9[1]), .out_11(substractor_four_2_out_9[2]),
    .out_12(substractor_four_2_out_12[0]));  // open: B3, A3
  Multiplexer multiplexer_1 (.in0(B3), .in1(A3), .out(multiplexer_1_out), .sel(substractor_four_2_out_12[1]));
  Multiplexer multiplexer_2 (.in0(and_1_out), .in1(multiplexer_1_out), .out(Y3), .sel(xor_1_out));
  Multiplexer #(.select(2), .width(3)) multiplexer_3 (
    .in0(substractor_four_1_out_9), .in1(substractor_four_1_out_9), .in2(substractor_four_2_out_9),
    .out(multiplexer_3_out), .sel(substractor_four_2_out_12));  // open: in3
  Multiplexer #(.width(3)) multiplexer_4 (
    .in0(four_add_1_out_9), .in1(multiplexer_3_out), .out({Y2, Y1, Y0}), .sel(xor_1_out));

  // Notes on the sheet:
  //   原码加法器
  //   加法器
  //   减法器
  //   减法器
endmodule
