// Logisim project Register_4bit.circ as structural Verilog: 5 circuits, main circuit D_Trigger_EN
module Register_for_4bit (
  input  A0,
  input  A1,
  input  A2,
  input  A3,
  input  CLK,
  input  Enable,
  input  RESET,
  output Y0,
  output Y1,
  output Y2,
  output Y3
);

  D_Trigger_EN d_trigger_en_1 (.CLK(CLK), .Enable(Enable), .RESET(RESET), .D(A0), .Q(Y0));  // open: NQ
  D_Trigger_EN d_trigger_en_2 (.CLK(CLK), .Enable(Enable), .RESET(RESET), .D(A1), .Q(Y1));  // open: NQ
  D_Trigger_EN d_trigger_en_3 (.CLK(CLK), .Enable(Enable), .RESET(RESET), .D(A2), .Q(Y2));  // open: NQ
  D_Trigger_EN d_trigger_en_4 (.CLK(CLK), .Enable(Enable), .RESET(RESET), .D(A3), .Q(Y3));  // open: NQ
endmodule

module D_Trigger_EN (
  input  D,
  input  CLK,
  input  Enable,
  input  RESET,
  output Q,
  output NQ
);

  wire and_1_out, multiplexer_1_out;

  and and_1 (and_1_out, RESET, D);
  Multiplexer multiplexer_1 (.in0(1'b1), .in1(and_1_out), .out(multiplexer_1_out), .sel(Enable));
  D_Trigger d_trigger_1 (.D(multiplexer_1_out), .CLK(CLK), .Q(Q), .NQ(NQ));
endmodule

module D_Trigger (
  input  D,
  input  CLK,
  output Q,
  output NQ
);

  wire d_latch_1_q, not_1_out;

  not not_1 (not_1_out, CLK);
  D_Latch d_latch_1 (.D(D), .Enable(not_1_out), .Q(d_latch_1_q));  // open: NQ
  D_Latch d_latch_2 (.D(d_latch_1_q), .Enable(CLK), .Q(Q), .NQ(NQ));
endmodule

module D_Latch (
  input  Enable,
  input  D,
  output Q,
  output NQ
);

  wire and_1_out, and_2_out, not_1_out;

  not not_1 (not_1_out, D);
  and and_1 (and_1_out, D, Enable);
  and and_2 (and_2_out, Enable, not_1_out);
  SR sr_1 (.S(and_1_out), .R(and_2_out), .Q(Q), .QW(NQ));
endmodule

module SR (
  input  S,
  input  R,
  output Q,
  output QW
);

  nor nor_1 (Q, R, QW);
  nor nor_2 (QW, Q, S);
endmodule
