// Logisim project D_FlipFlop.circ as structural Verilog: 1 circuit, main circuit main
module main (
  input  CLK,
  input  D,
  output Q,
  output Qfan
);

  wire nor_1_out, nor_2_out, not_1_out;

  not not_1 (not_1_out, CLK);
  nor nor_1 (nor_1_out, CLK, nor_2_out);
  nor nor_2 (nor_2_out, nor_1_out, D);
  nor nor_3 (Q, not_1_out, Qfan);
  nor nor_4 (Qfan, Q, nor_2_out);
endmodule
