// Logisim project D_Latch.circ as structural Verilog: 1 circuit, main circuit main
module main (
  input  WE,
  input  D,
  output Q,
  output Qfan
);

  wire and_1_out, and_2_out, not_1_out;

  not not_1 (not_1_out, D);
  and and_1 (and_1_out, D, WE);
  and and_2 (and_2_out, WE, not_1_out);
  or or_1 (Q, and_1_out, Qfan);
  or or_2 (Qfan, Q, and_2_out);
endmodule
