// Logisim project SR.circ as structural Verilog: 1 circuit, main circuit main
module main (
  input  S,
  input  R,
  output Q,
  output QW
);

  nor nor_1 (Q, S, QW);
  nor nor_2 (QW, Q, R);
endmodule
