// Logisim project shumaguan10_16.circ as structural Verilog: 3 circuits, main circuit main
module main (
  input  D3,
  input  D2,
  input  D1,
  input  D0
);

  wire [6:0] and_1_out, kong7_10_1_a, kong7_16_1_a;

  kong7_10 kong7_10_1 (
    .A3(D3), .A2(D2), .A1(D1), .A0(D0), .a(kong7_10_1_a[0]), .b(kong7_10_1_a[1]), .c(kong7_10_1_a[2]),
    .d(kong7_10_1_a[3]), .e(kong7_10_1_a[4]), .f(kong7_10_1_a[5]), .g(kong7_10_1_a[6]));
  kong7_16 kong7_16_1 (
    .y1(D3), .y2(D2), .y3(D1), .y4(D0), .A(kong7_16_1_a[0]), .B(kong7_16_1_a[1]), .C(kong7_16_1_a[2]),
    .D(kong7_16_1_a[3]), .E(kong7_16_1_a[4]), .F(kong7_16_1_a[5]), .G(kong7_16_1_a[6]));
  assign and_1_out = kong7_10_1_a & kong7_16_1_a;  // AND_Gate and_1, 7 bits wide
  _7_Segment_Display u_7_segment_display_1 (
    .g(and_1_out[6]), .f(and_1_out[5]), .a(and_1_out[0]), .b(and_1_out[1]), .e(and_1_out[4]),
    .d(and_1_out[3]), .c(and_1_out[2]));  // open: dp
endmodule

module kong7_10 (
  input  A3,
  input  A2,
  input  A1,
  input  A0,
  output a,
  output b,
  output c,
  output d,
  output e,
  output f,
  output g
);

  wire and_1_out, and_2_out, and_3_out, and_4_out, and_5_out, and_6_out, and_7_out, and_8_out, and_9_out,
       and_10_out, and_11_out, and_12_out, and_13_out, and_14_out, and_15_out, and_16_out, and_17_out,
       and_18_out, and_19_out, and_20_out, and_21_out, and_22_out, and_23_out, and_24_out, and_25_out,
       and_26_out, and_27_out, and_28_out, and_29_out, and_30_out, and_31_out, and_32_out, and_33_out,
       not_1_out, not_2_out, not_3_out, not_4_out;

  not not_1 (not_1_out, A3);
  not not_2 (not_2_out, A2);
  not not_3 (not_3_out, A1);
  not not_4 (not_4_out, A0);
  and and_1 (and_1_out, not_2_out, not_4_out);
  and and_2 (and_2_out, not_1_out, A1);
  and and_3 (and_3_out, A2, A0);
  and and_4 (and_4_out, A3, not_3_out);
  and and_5 (and_5_out, not_3_out, not_4_out);
  and and_6 (and_6_out, not_1_out, A1, A0);
  and and_7 (and_7_out, A3, not_3_out);
  and and_8 (and_8_out, A3, not_4_out);
  and and_9 (and_9_out, not_1_out, not_3_out);
  and and_10 (and_10_out, not_1_out, A2);
  and and_11 (and_11_out, not_2_out, not_3_out);
  and and_12 (and_12_out, A3, not_2_out);
  and and_13 (and_13_out, A2, A1);
  and and_14 (and_14_out, not_2_out, not_4_out);
  and and_15 (and_15_out, not_1_out, not_2_out, A1);
  and and_16 (and_16_out, A2, not_3_out, A0);
  and and_17 (and_17_out, not_1_out, A1, not_4_out);
  and and_18 (and_18_out, A3, not_3_out);
  and and_19 (and_19_out, A3, A2, A0);
  and and_20 (and_20_out, not_2_out, not_4_out);
  and and_21 (and_21_out, not_1_out, A1, not_4_out);
  and and_22 (and_22_out, A3, not_3_out, not_4_out);
  and and_23 (and_23_out, not_1_out, A2, not_3_out);
  and and_24 (and_24_out, A3, not_2_out, not_3_out);
  and and_25 (and_25_out, A3, A2, A1);
  and and_26 (and_26_out, not_1_out, not_3_out, not_4_out);
  and and_27 (and_27_out, not_1_out, A2, not_4_out);
  and and_28 (and_28_out, A3, not_2_out, not_4_out);
  and and_29 (and_29_out, not_1_out, not_2_out, A1);
  and and_30 (and_30_out, A2, not_3_out);
  and and_31 (and_31_out, A3, not_3_out);
  and and_32 (and_32_out, A3, A2);
  and and_33 (and_33_out, not_1_out, A1, not_4_out);
  or or_1 (a, and_1_out, and_2_out, and_3_out, and_4_out);
  or or_2 (b, not_2_out, and_5_out, and_6_out, and_7_out, and_8_out);
  or or_3 (c, A0, and_9_out, and_10_out, and_11_out, and_12_out, and_13_out);
  or or_4 (d, and_14_out, and_15_out, and_16_out, and_17_out, and_18_out, and_19_out);
  or or_5 (e, and_20_out, and_21_out, and_22_out);
  or or_6 (f, and_23_out, and_24_out, and_25_out, and_26_out, and_27_out, and_28_out);
  or or_7 (g, and_29_out, and_30_out, and_31_out, and_32_out, and_33_out);
endmodule

module kong7_16 (
  input  y1,
  input  y2,
  input  y3,
  input  y4,
  output A,
  output B,
  output C,
  output D,
  output E,
  output F,
  output G
);

  wire and_1_out, and_2_out, and_3_out, and_4_out, and_5_out, and_6_out, and_7_out, and_8_out, and_9_out,
       and_10_out, and_11_out, and_12_out, and_13_out, and_14_out, and_15_out, and_16_out, and_17_out,
       and_18_out, and_19_out, and_20_out, and_21_out, and_22_out, and_23_out, and_24_out, and_25_out,
       and_26_out, and_27_out, and_28_out, and_29_out, and_30_out, and_31_out, and_32_out, and_33_out,
       and_34_out, and_35_out, and_36_out, and_37_out, and_38_out, and_39_out, and_40_out, not_1_out,
       not_2_out, not_3_out, not_4_out;

  not not_1 (not_1_out, y1);
  not not_2 (not_2_out, y2);
  not not_3 (not_3_out, y3);
  not not_4 (not_4_out, y4);
  and and_1 (and_1_out, not_2_out, not_4_out);
  and and_2 (and_2_out, not_1_out, y3);
  and and_3 (and_3_out, not_1_out, y2, y4);
  and and_4 (and_4_out, y1, not_2_out, not_3_out);
  and and_5 (and_5_out, y1, not_4_out);
  and and_6 (and_6_out, y2, y3);
  and and_7 (and_7_out, not_1_out, not_3_out, not_4_out);
  and and_8 (and_8_out, not_1_out, y3, y4);
  and and_9 (and_9_out, not_2_out, not_4_out);
  and and_10 (and_10_out, y1, not_3_out, y4);
  and and_11 (and_11_out, not_1_out, not_2_out);
  and and_12 (and_12_out, not_1_out, y2);
  and and_13 (and_13_out, y1, not_2_out);
  and and_14 (and_14_out, not_3_out, y4);
  and and_15 (and_15_out, not_1_out, not_3_out);
  and and_16 (and_16_out, not_1_out, y4);
  and and_17 (and_17_out, y2, not_3_out, y4);
  and and_18 (and_18_out, not_1_out, not_2_out, not_4_out);
  and and_19 (and_19_out, not_1_out, not_2_out, y3);
  and and_20 (and_20_out, not_1_out, y3, not_4_out);
  and and_21 (and_21_out, not_2_out, not_3_out, not_4_out);
  and and_22 (and_22_out, y1, not_2_out, y4);
  and and_23 (and_23_out, y1, not_3_out);
  and and_24 (and_24_out, y2, y3, not_4_out);
  and and_25 (and_25_out, not_2_out, not_4_out);
  and and_26 (and_26_out, y3, not_4_out);
  and and_27 (and_27_out, y1, y3);
  and and_28 (and_28_out, y1, y2);
  and and_29 (and_29_out, not_3_out, not_4_out);
  and and_30 (and_30_out, not_1_out, y2, not_3_out);
  and and_31 (and_31_out, y2, not_4_out);
  and and_32 (and_32_out, y1, not_2_out);
  and and_33 (and_33_out, y1, y3);
  and and_34 (and_34_out, not_2_out, y3);
  and and_35 (and_35_out, y1, not_2_out);
  and and_36 (and_36_out, not_1_out, y2, not_3_out);
  and and_37 (and_37_out, not_1_out, y2, not_4_out);
  and and_38 (and_38_out, y2, not_3_out, y4);
  and and_39 (and_39_out, y3, not_4_out);
  and and_40 (and_40_out, y1, y4);
  or or_1 (A, and_1_out, and_2_out, and_3_out, and_4_out, and_5_out, and_6_out);
  or or_2 (B, and_7_out, and_8_out, and_9_out, and_10_out, and_11_out);
  or or_3 (C, and_12_out, and_13_out, and_14_out, and_15_out, and_16_out);
  or or_4 (D, and_17_out, and_18_out, and_19_out, and_20_out, and_21_out, and_22_out, and_23_out, and_24_out);
  or or_5 (E, and_25_out, and_26_out, and_27_out, and_28_out);
  or or_6 (F, and_29_out, and_30_out, and_31_out, and_32_out, and_33_out);
  or or_7 (G, and_34_out, and_35_out, and_36_out, and_37_out, and_38_out, and_39_out, and_40_out);
endmodule
